// Logisim project TrafficLightProject .circ as structural Verilog: 2 circuits, main circuit Z2
module Z2 (
);

  wire and_1_out, and_2_out, and_3_out, and_4_out, and_5_out, and_6_out, clock_1_out, or_1_out, or_2_out,
       or_3_out, t_ff_1_q, t_ff_1_qn, t_ff_2_q, t_ff_2_qn, t_ff_3_q, t_ff_3_qn, t_ff_4_q, t_ff_4_qn;

  Clock clock_1 (.out(clock_1_out));
  LED led_1 (.in(t_ff_1_qn));
  LED led_2 (.in(and_2_out));
  LED led_3 (.in(and_1_out));
  and and_1 (and_1_out, or_1_out, t_ff_1_q);
  T_Flip_Flop t_ff_1 (.T(and_2_out), .clk(clock_1_out), .Q(t_ff_1_q), .Qn(t_ff_1_qn));  // open: reset, preset
  and and_2 (and_2_out, t_ff_2_q, t_ff_4_q);
  or or_1 (or_1_out, t_ff_3_qn, t_ff_2_qn);
  T_Flip_Flop t_ff_2 (.T(and_3_out), .clk(clock_1_out), .Q(t_ff_2_q), .Qn(t_ff_2_qn));  // open: reset, preset
  and and_3 (and_3_out, t_ff_3_q, t_ff_4_q);
  or or_2 (or_2_out, t_ff_4_q, t_ff_2_q);
  T_Flip_Flop t_ff_3 (.T(or_2_out), .clk(clock_1_out), .Q(t_ff_3_q), .Qn(t_ff_3_qn));  // open: reset, preset
  T_Flip_Flop t_ff_4 (.T(1'b1), .clk(clock_1_out), .Q(t_ff_4_q), .Qn(t_ff_4_qn));  // open: reset, preset
  and and_4 (and_4_out, t_ff_2_q, t_ff_3_q);
  LED led_4 (.in(t_ff_1_q));
  LED led_5 (.in(and_4_out));
  LED led_6 (.in(or_3_out));
  and and_5 (and_5_out, t_ff_1_qn, t_ff_2_qn);
  and and_6 (and_6_out, t_ff_3_qn, t_ff_1_qn, t_ff_2_q);
  or or_3 (or_3_out, and_5_out, and_6_out);
endmodule

module Z3 (
  input  alt,
  input  enable
);

  wire and_1_out, and_2_out, and_3_out, and_4_out, and_5_out, and_6_out, and_7_out, and_8_out, and_9_out,
       and_10_out, clock_1_out, d_ff_1_q, d_ff_1_qn, d_ff_2_q, d_ff_2_qn, d_ff_3_q, d_ff_3_qn, or_1_out,
       or_2_out, or_3_out, or_4_out, or_5_out, or_6_out, or_7_out, xor_1_out;

  Clock clock_1 (.out(clock_1_out));
  or or_1 (or_1_out, ~enable, alt);  // OR_Gate
  D_Flip_Flop d_ff_1 (.D(or_1_out), .clk(clock_1_out), .Q(d_ff_1_q), .Qn(d_ff_1_qn));  // open: preset, reset
  D_Flip_Flop d_ff_2 (.D(or_2_out), .clk(clock_1_out), .Q(d_ff_2_q), .Qn(d_ff_2_qn));  // open: preset, reset
  or or_2 (or_2_out, ~enable, and_1_out);  // OR_Gate
  and and_1 (and_1_out, ~alt, d_ff_1_qn, d_ff_3_q);  // AND_Gate
  D_Flip_Flop d_ff_3 (.D(or_3_out), .clk(clock_1_out), .Q(d_ff_3_q), .Qn(d_ff_3_qn));  // open: preset, reset
  and and_2 (and_2_out, ~alt, d_ff_1_qn, d_ff_2_qn);  // AND_Gate
  and and_3 (and_3_out, alt, d_ff_1_q, d_ff_2_qn, d_ff_3_qn);
  or or_3 (or_3_out, ~enable, and_2_out, and_3_out);  // OR_Gate
  and and_4 (and_4_out, d_ff_2_q, d_ff_1_qn);
  and and_5 (and_5_out, d_ff_1_q, d_ff_3_qn);
  and and_6 (and_6_out, d_ff_3_qn, d_ff_2_qn);
  and and_7 (and_7_out, d_ff_1_qn, d_ff_2_qn);
  or or_4 (or_4_out, and_7_out, and_8_out);
  and and_8 (and_8_out, d_ff_1_q, d_ff_3_qn);
  or or_5 (or_5_out, d_ff_1_q, d_ff_2_q);
  xor xor_1 (xor_1_out, or_5_out, d_ff_3_q);
  and and_9 (and_9_out, d_ff_3_qn, d_ff_1_q);
  or or_6 (or_6_out, and_9_out, and_10_out);
  and and_10 (and_10_out, d_ff_3_q, d_ff_2_q, d_ff_1_qn);
  or or_7 (or_7_out, and_4_out, and_5_out);
  LED led_1 (.in(or_7_out));
  LED led_2 (.in(xor_1_out));
  LED led_3 (.in(and_6_out));
  LED led_4 (.in(or_4_out));
  LED led_5 (.in(xor_1_out));
  LED led_6 (.in(or_6_out));
endmodule
